# Fritzing sketch home automation (saved by Fritzing 0.9.3b)
circuit board: 8.46667cm x 5.64444cm
breadboards: 1

parts:
  LED1 = LED - 5mm [color="Green (565nm)" package="5 mm [THT]"]
  DHT11 = DHT11 Humitidy and Temperature Sensor
  Relay = songle relay
  Resistor = Resistor [tolerance=±5% resistance=220 package=THT]
  FC-1 = Sound Sensor
  DC_Motor = DC Motor
  6V_DC_power_source = 4 x AA Battery Box
  Part1 = Arduino Mega ADK (Rev3)

nets:
  N1: LED1.cathode, FC-1.GND
  N2: LED1.anode, Resistor.Pin_0
  VCC: DHT11.VDD, Relay.VCC, FC-1.VCC, Part1.IOREF, Part1.5V
  N3: DHT11.DATA, Part1.D7_PWM
  GND: DHT11.GND, Relay.GND
  N4: Relay.NO, DC_Motor.pin_1
  N5: Relay.NC, 6V_DC_power_source.+
  N6: Relay.COMMON, Part1.D6_PWM
  N7: Resistor.Pin_1, Part1.D4_PWM
  N8: FC-1.OUT, Part1.A1
  N9: DC_Motor.pin_2, 6V_DC_power_source.-, Part1.GND

custom parts:
  DHT11 Humitidy and Temperature Sensor: DHT11 Humidity and Temperature Sensor
  4 x AA Battery Box: A 4 x AA battery box.

// code stored in the sketch: Untitled2.ino
#include <dht_nonblocking.h>
#define DHT_SENSOR_TYPE DHT_TYPE_11

static const int DHT_SENSOR_PIN = 7;
int soundSensorPin = A1;

int fanPin = 6;
int ledPin = 4;

int ledStatus = 0;

DHT_nonblocking dht_sensor( DHT_SENSOR_PIN, DHT_SENSOR_TYPE );




void setup() {
  // put your setup code here, to run once:
  pinMode(ledPin, OUTPUT);
  pinMode(fanPin, OUTPUT);
  pinMode(soundSensorPin, INPUT);
  
  Serial.begin(9600);
  

}

static bool measure_environment( float *temperature, float *humidity )
{
  static unsigned long measurement_timestamp = millis( );

  /* Measure once every four seconds. */
  if( millis( ) - measurement_timestamp > 3000ul )
  {
    if( dht_sensor.measure( temperature, humidity ) == true )
    {
      measurement_timestamp = millis( );
      return( true );
    }
  }

  return( false );
}

void loop() {
  Serial.println("bla bla");
  // put your main code here, to run repeatedly:
  float temperature;
  float humidity;
  
  int sound = analogRead(soundSensorPin);
  

  
    if(ledStatus == 0 && sound >= 100){
      digitalWrite(ledPin, HIGH);
      ledStatus = 1;
      //Serial.println(sound);
      sound = 0;
      delay(1000);
    }
    
    if (ledStatus == 1 && sound >= 100){
      digitalWrite(ledPin, LOW);
      ledStatus = false;
     // Serial.println(sound);
      delay(1000);
    
    }


  if((measure_environment( &temperature, &humidity ) )== true )
  {
    Serial.print( "T = " );
    Serial.print( temperature, 1 );
    Serial.print( " deg. C, H = " );
    Serial.print( humidity, 1 );
    Serial.println( "%" );
 
    if(temperature >= 29.0){
      digitalWrite(fanPin, HIGH);
    }else {
      digitalWrite(fanPin, LOW);
      }
  }


}
